# Fritzing sketch ugv (saved by Fritzing 1.0.2b)

parts:
  J1 = double row male pin header, 6 pins [form="♂ (male)"]
  J2 = shrouded pin header, 32 pins [form="♂ (shrouded male)"]
  J4 = Screw terminal - 2 pins [package=THT]
  J5 = screw terminal, 3 pins  # not connected
  M1 = DC Motor [voltage_(max)=6V voltage_(min)=3V]
  M2 = DC Motor [voltage_(max)=6V voltage_(min)=3V]
  J3 = Screw terminal - 2 pins [package=THT]
  Raspberry_Pi1 = Raspberry Pi B+

nets:
  N1: J1.pin1, Raspberry_Pi1.GPIO13
  N2: J1.pin2, Raspberry_Pi1.GPIO24
  N3: J1.pin3, Raspberry_Pi1.GPIO23
  N4: J1.pin4, Raspberry_Pi1.GPIO22
  N5: J1.pin5, Raspberry_Pi1.GPIO17
  N6: J1.pin6, Raspberry_Pi1.GPIO18
  N7: J2.pin1, Raspberry_Pi1.5V
  N8: J2.pin30, J2.pin31, J2.pin32, Raspberry_Pi1.GND
  N9: J4.pin1, M2.pin_2
  N10: J4.pin2, M2.pin_1
  N11: M1.pin_1, J3.pin2
  N12: M1.pin_2, J3.pin1
